// Logisim project Project.circ as structural Verilog
module register_file (
  input  [31:0] WriteData,
  input  [3:0] WriteRegister,
  input  CLK,
  input  WriteEnable,
  input  [3:0] ReadRegister1,
  input  [3:0] ReadRegister2,
  output [31:0] ReadData1,
  output [31:0] ReadData2
);

  wire and_1_out, and_2_out, and_3_out, and_4_out, and_5_out, and_6_out, and_7_out, and_8_out, and_9_out,
       and_10_out, and_11_out, and_12_out, and_13_out, and_14_out, and_15_out, and_16_out, decoder_1_out0,
       decoder_1_out1, decoder_1_out2, decoder_1_out3, decoder_1_out4, decoder_1_out5, decoder_1_out6,
       decoder_1_out7, decoder_1_out8, decoder_1_out9, decoder_1_out10, decoder_1_out11, decoder_1_out12,
       decoder_1_out13, decoder_1_out14, decoder_1_out15;
  wire [31:0] R0_q, R1_q, R2_q, R3_q, R4_q, R5_q, R6_q, R7_q, R8_q, R9_q, R10_q, R11_q, R12_q, R13_q, R14_q,
       R15_q;

  and and_1 (and_1_out, decoder_1_out0, WriteEnable);
  and and_2 (and_2_out, decoder_1_out1, WriteEnable);
  and and_3 (and_3_out, decoder_1_out2, WriteEnable);
  and and_4 (and_4_out, decoder_1_out3, WriteEnable);
  Register #(.width(32)) R0 (.D(WriteData), .en(and_1_out), .Q(R0_q), .clk(CLK));  // open: clr
  Register #(.width(32)) R1 (.D(WriteData), .en(and_2_out), .Q(R1_q), .clk(CLK));  // open: clr
  Register #(.width(32)) R2 (.D(WriteData), .en(and_3_out), .Q(R2_q), .clk(CLK));  // open: clr
  Register #(.width(32)) R3 (.D(WriteData), .en(and_4_out), .Q(R3_q), .clk(CLK));  // open: clr
  and and_5 (and_5_out, decoder_1_out4, WriteEnable);
  and and_6 (and_6_out, decoder_1_out5, WriteEnable);
  and and_7 (and_7_out, decoder_1_out6, WriteEnable);
  and and_8 (and_8_out, decoder_1_out7, WriteEnable);
  Decoder #(.select(4)) decoder_1 (
    .out0(decoder_1_out0), .out1(decoder_1_out1), .out2(decoder_1_out2), .out3(decoder_1_out3),
    .out4(decoder_1_out4), .out5(decoder_1_out5), .out6(decoder_1_out6), .out7(decoder_1_out7),
    .out8(decoder_1_out8), .out9(decoder_1_out9), .out10(decoder_1_out10), .out11(decoder_1_out11),
    .out12(decoder_1_out12), .out13(decoder_1_out13), .out14(decoder_1_out14), .out15(decoder_1_out15),
    .sel(WriteRegister));  // open: en
  Register #(.width(32)) R4 (.D(WriteData), .en(and_5_out), .Q(R4_q), .clk(CLK));  // open: clr
  Register #(.width(32)) R5 (.D(WriteData), .en(and_6_out), .Q(R5_q), .clk(CLK));  // open: clr
  Register #(.width(32)) R6 (.D(WriteData), .en(and_7_out), .Q(R6_q), .clk(CLK));  // open: clr
  Register #(.width(32)) R7 (.D(WriteData), .en(and_8_out), .Q(R7_q), .clk(CLK));  // open: clr
  and and_9 (and_9_out, decoder_1_out8, WriteEnable);
  and and_10 (and_10_out, decoder_1_out9, WriteEnable);
  and and_11 (and_11_out, decoder_1_out10, WriteEnable);
  and and_12 (and_12_out, decoder_1_out11, WriteEnable);
  Register #(.width(32)) R8 (.D(WriteData), .en(and_9_out), .Q(R8_q), .clk(CLK));  // open: clr
  Register #(.width(32)) R9 (.D(WriteData), .en(and_10_out), .Q(R9_q), .clk(CLK));  // open: clr
  Register #(.width(32)) R10 (.D(WriteData), .en(and_11_out), .Q(R10_q));  // open: clk, clr
  Register #(.width(32)) R11 (.D(WriteData), .en(and_12_out), .Q(R11_q));  // open: clk, clr
  Multiplexer #(.select(4), .width(32)) multiplexer_1 (
    .in0(R0_q), .in1(R1_q), .in2(R2_q), .in3(R3_q), .in4(R4_q), .in5(R5_q), .in6(R6_q), .in7(R7_q),
    .in8(R8_q), .in9(R9_q), .in10(R10_q), .in11(R11_q), .in12(R12_q), .in13(R13_q), .in14(R14_q),
    .in15(R15_q), .out(ReadData1), .sel(ReadRegister1));  // open: en
  and and_13 (and_13_out, decoder_1_out12, WriteEnable);
  and and_14 (and_14_out, decoder_1_out13, WriteEnable);
  and and_15 (and_15_out, decoder_1_out14, WriteEnable);
  and and_16 (and_16_out, decoder_1_out15, WriteEnable);
  Register #(.width(32)) R12 (.D(WriteData), .en(and_13_out), .Q(R12_q), .clk(CLK));  // open: clr
  Register #(.width(32)) R13 (.D(WriteData), .en(and_14_out), .Q(R13_q), .clk(CLK));  // open: clr
  Register #(.width(32)) R14 (.D(WriteData), .en(and_15_out), .Q(R14_q), .clk(CLK));  // open: clr
  Register #(.width(32)) R15 (.D(WriteData), .en(and_16_out), .Q(R15_q), .clk(CLK));  // open: clr
  Multiplexer #(.select(4), .width(32)) multiplexer_2 (
    .in0(R0_q), .in1(R1_q), .in2(R2_q), .in3(R3_q), .in4(R4_q), .in5(R5_q), .in6(R6_q), .in7(R7_q),
    .in8(R8_q), .in9(R9_q), .in10(R10_q), .in11(R11_q), .in12(R12_q), .in13(R13_q), .in14(R14_q),
    .in15(R15_q), .out(ReadData2), .sel(ReadRegister2));  // open: en
endmodule

module alu (
  input  Cin,
  input  [31:0] A,
  input  Binv,
  input  [2:0] ALUop,
  input  [31:0] B,
  output [31:0] ALUresult,
  output Cout,
  output Zero
);

  wire comparator_1_lt;
  wire [4:0] bit_extender_1_out;
  wire [7:0] bit_extender_2_out, bit_extender_3_out;
  wire [31:0] adder_1_out, and_1_out, bit_extender_4_out, multiplexer_1_out, not_1_out, shifter_1_out;

  assign not_1_out = ~B;  // NOT_Gate not_1, 32 bits wide
  Multiplexer #(.width(32)) multiplexer_1 (.in0(B), .in1(not_1_out), .out(multiplexer_1_out), .sel(Binv));  // open: en
  Bit_Extender #(.in_width(32), .out_width(5)) bit_extender_1 (.in(B), .out(bit_extender_1_out));
  Bit_Extender #(.in_width(32), .out_width(8)) bit_extender_2 (.in(A), .out(bit_extender_2_out));
  Bit_Extender #(.in_width(32), .out_width(8)) bit_extender_3 (.in(B), .out(bit_extender_3_out));
  Shifter #(.width(32)) shifter_1 (.in(A), .\dist (bit_extender_1_out), .out(shifter_1_out));
  Comparator comparator_1 (.a(bit_extender_2_out), .b(bit_extender_3_out), .lt(comparator_1_lt));  // open: gt, eq
  Adder #(.width(32)) adder_1 (.a(A), .b(multiplexer_1_out), .out(adder_1_out), .cin(Cin), .cout(Cout));
  assign and_1_out = A & B;  // AND_Gate and_1, 32 bits wide
  assign bit_extender_4_out = {{31{1'b0}}, comparator_1_lt};  // Bit_Extender bit_extender_4
  nor nor_1 (Zero, ALUresult[0], ALUresult[1], ALUresult[2], ALUresult[3], ALUresult[4], ALUresult[5], ALUresult[6], ALUresult[7], ALUresult[8], ALUresult[9], ALUresult[10], ALUresult[11], ALUresult[12], ALUresult[13], ALUresult[14], ALUresult[15], ALUresult[17], ALUresult[18], ALUresult[19], ALUresult[20], ALUresult[21], ALUresult[22], ALUresult[23], ALUresult[24], ALUresult[25], ALUresult[26], ALUresult[27], ALUresult[28], ALUresult[29], ALUresult[30], ALUresult[31], ALUresult[16]);
  Multiplexer #(.select(3), .width(32)) multiplexer_2 (
    .in0(A), .in1(adder_1_out), .in2(and_1_out), .in3(shifter_1_out), .in4(bit_extender_4_out), .in5(A),
    .in6(A), .in7(A), .out(ALUresult), .sel(ALUop));  // open: en

  // Notes on the sheet:
  //   and 010
  //   sll 011
  //   slt 100
  //   nop, beq, jmp 000
  //   add, addi, sub, lw, sw 001
endmodule

module control_unit (
  input  [3:0] OPcode,
  output Binv,
  output Mem2Reg,
  output Cin,
  output WriteReg,
  output ALUsrc,
  output [2:0] ALUop,
  output RegDst,
  output Str_MemRead,
  output Ld_MemWrite
);

  wire decoder_1_out0, decoder_1_out1, decoder_1_out2, decoder_1_out3, decoder_1_out4, decoder_1_out7,
       decoder_1_out8, decoder_1_out11, decoder_1_out12, decoder_1_out13, decoder_1_out14, decoder_1_out15;

  or or_1 (ALUsrc, decoder_1_out1, Ld_MemWrite, Str_MemRead);
  or or_2 (RegDst, decoder_1_out1, Ld_MemWrite);
  Decoder #(.select(4)) decoder_1 (
    .out0(decoder_1_out0), .out1(decoder_1_out1), .out2(decoder_1_out2), .out3(decoder_1_out3),
    .out4(decoder_1_out4), .out5(Binv), .out6(Ld_MemWrite), .out7(decoder_1_out7), .out8(decoder_1_out8),
    .out9(ALUop[2]), .out10(Str_MemRead), .out11(decoder_1_out11), .out12(decoder_1_out12),
    .out13(decoder_1_out13), .out14(decoder_1_out14), .out15(decoder_1_out15), .sel(OPcode));  // open: en
  or or_3 (WriteReg, decoder_1_out0, decoder_1_out1, decoder_1_out2, decoder_1_out3, Binv, Ld_MemWrite, ALUop[2], decoder_1_out8);
  or or_4 (ALUop[1], decoder_1_out2, decoder_1_out8);
  or or_5 (ALUop[0], Binv, decoder_1_out1, decoder_1_out3, Ld_MemWrite, decoder_1_out8, Str_MemRead);

  assign Cin = Binv;
  assign Mem2Reg = Ld_MemWrite;
endmodule
